// Logisim project A4.circ as structural Verilog: 5 circuits, main circuit main
module main (
  input  in_1,
  input  in_2,
  input  in_3,
  input  in_4,
  input  in_5,
  input  [31:0] in_6,
  input  in_7,
  input  in_8,
  input  in_9,
  input  in_10,
  input  in_11,
  input  in_12,
  input  in_13,
  input  in_14,
  input  in_15,
  input  [31:0] in_16,
  input  in_17,
  input  in_18,
  input  in_19,
  input  in_20,
  input  [2:0] in_21,
  input  in_22,
  input  in_23,
  input  in_24,
  input  in_25,
  input  in_26,
  input  in_27,
  input  in_28,
  input  in_29,
  input  in_30,
  input  in_31,
  input  in_32,
  output [31:0] out_33,
  output [31:0] out_34
);

  wire ADD, ADI, AND, ANI, clk, clock_1_out, HLT, LOAD, MOV, MVI, OR, ORI, READ_MEM, STORE, SUB, SUI;
  wire [3:0] OPCODE, Select_RA, Select_RB, Select_RY;
  wire [15:0] MEM_IN;
  wire [31:0] adder_1_out, alu_1_alu_out, FETCH_OUT, Immediate, MEM_OUT, multiplexer_1_out,
       multiplexer_2_out, RA_q, RB_q, registerfile_1_ra, registerfile_1_rb, RM_OUT, RZ_OUT;
  wire [31:16] multiplexer_3_out;

  or or_1 (clk, in_1, clock_1_out);
  Button RESET (.out(in_1));
  Clock clock_1 (.out(clock_1_out));
  RegisterFile registerfile_1 (
    .RA(registerfile_1_ra), .Address_RA(Select_RA), .RB(registerfile_1_rb), .Address_RB(Select_RB),
    .RY(in_6), .clk(clk), .enRA(in_2), .enRB(in_4), .enRY(in_5), .clr(in_1), .Address_RY(Select_RY),
    .SELECT_STORE_MUX(in_7));
  Register #(.width(32)) RA (.D(registerfile_1_ra), .en(in_8), .Q(RA_q), .clk(clk), .clr(in_1));
  Register #(.width(32)) RB (.D(registerfile_1_rb), .en(in_9), .Q(RB_q), .clk(clk), .clr(in_1));
  ALU alu_1 (
    .ALU_Out(alu_1_alu_out), .ALU_Enable(in_22), .InputRA(RA_q), .InputRB(multiplexer_1_out),
    .ALU_Select(in_21));
  Register #(.width(32)) RZ (.D(alu_1_alu_out), .en(in_14), .Q(RZ_OUT), .clk(clk), .clr(in_1));
  Multiplexer #(.width(32)) multiplexer_1 (
    .in0(RB_q), .in1(Immediate), .out(multiplexer_1_out), .sel(in_24), .en(in_23));
  Multiplexer #(.width(32)) multiplexer_2 (
    .in0(RZ_OUT), .in1(MEM_OUT), .out(multiplexer_2_out), .sel(in_18), .en(in_17));
  Register #(.width(32)) RY (.D(multiplexer_2_out), .en(in_19), .Q(in_6), .clk(clk), .clr(in_1));
  Register #(.width(32)) RM (.D(RB_q), .en(in_12), .Q(RM_OUT), .clk(clk), .clr(in_1));
  Register #(.width(32)) PC (.D(adder_1_out), .en(in_27), .Q(FETCH_OUT), .clk(clk), .clr(in_1));
  Multiplexer #(.width(32), .enable("false")) multiplexer_3 (
    .in0(FETCH_OUT), .in1(RZ_OUT), .out({multiplexer_3_out, MEM_IN}), .sel(in_30));
  InstructionRegister instructionregister_1 (
    .EN_IR(in_31), .INPUT_IR(MEM_OUT), .clk(clk), .CLR_IR(in_1), .OPCODE(OPCODE), .SELECT_RY(Select_RY),
    .SELECT_RA(Select_RA), .SELECT_RB(Select_RB), .IMMEDIATE(Immediate));
  RAM #(.addrWidth(16), .dataWidth(32), .bus("separate")) ram_1 (
    .addr(MEM_IN), .din(RM_OUT), .data(MEM_OUT), .str(in_26), .sel(1'b1), .clk(clk), .ld(READ_MEM),
    .clr(in_25));
  Adder #(.width(32)) adder_1 (.a(FETCH_OUT), .b(32'h1), .out(adder_1_out), .cin(in_3));  // open: cout
  Decoder #(.select(4)) decoder_1 (
    .out0(ADD), .out1(SUB), .out2(AND), .out3(OR), .out4(MOV), .out5(LOAD), .out6(STORE), .out7(MVI),
    .out8(ADI), .out9(SUI), .out10(ANI), .out11(ORI), .out12(HLT), .sel(OPCODE), .en(1'b1));  // open: out13, out14, out15
  not not_1 (READ_MEM, in_26);

  assign in_10 = in_1;
  assign in_11 = in_1;
  assign in_13 = in_1;
  assign in_15 = in_1;
  assign in_20 = in_1;
  assign in_28 = in_1;
  assign in_32 = in_1;

  // Other names for the same wires on the sheet: ALU_Out[31:0] = out_34; CLR_MEM = in_25; CLR_IR = in_1;
  //   CLR_PC = in_1; CLR_RA = in_1; CLR_RB = in_1; CLR_RF = in_1; CLR_RM = in_1; CLR_RY = in_1; CLR_RZ = in_1;
  //   EN_ALU = in_22; EN_IR = in_31; EN_MUX_B = in_23; EN_MUX_MEM = in_29; EN_MUX_Y = in_17; EN_PC = in_27;
  //   EN_RA = in_8; EN_RB = in_9; EN_RM = in_12; EN_RY = in_19; EN_RZ = in_14; EN_Select_RA = in_2;
  //   EN_Select_RB = in_4; EN_Select_RY = in_5; MEM_ADDRESS[31:0] = out_33; MEM_DATA[31:0] = in_16; RY[31:0] = in_6;
  //   Select_ALU[2:0] = in_21; Select_MUX_B = in_24; Select_MUX_MEM = in_30; Select_MUX_Y = in_18;
  //   STORE_SELECT_MUX = in_7; WRITE_MEM = in_26

  // Notes on the sheet:
  //   19CS01065
  //   Main File
  //   INSTRUCTION
  //   DECODER
endmodule

module RegisterFile (
  input  [3:0] Address_RY,
  input  enRA,
  input  [3:0] Address_RA,
  input  enRY,
  input  enRB,
  input  SELECT_STORE_MUX,
  input  [3:0] Address_RB,
  input  clk,
  input  clr,
  input  [31:0] RY,
  output [31:0] RA,
  output [31:0] RB
);

  wire demultiplexer_1_out0, demultiplexer_1_out1, demultiplexer_1_out2, demultiplexer_1_out3,
       demultiplexer_1_out4, demultiplexer_1_out5, demultiplexer_1_out6, demultiplexer_1_out7;
  wire [2:0] multiplexer_3_out;
  wire [3:3] multiplexer_3_out_2;
  wire [31:0] R1_q, R2_q, R3_q, R4_q, R5_q, R6_2_q, R6_q, R7_q;

  Demultiplexer #(.select(3)) demultiplexer_1 (
    .out0(demultiplexer_1_out0), .out1(demultiplexer_1_out1), .out2(demultiplexer_1_out2),
    .out3(demultiplexer_1_out3), .out4(demultiplexer_1_out4), .out5(demultiplexer_1_out5),
    .out6(demultiplexer_1_out6), .out7(demultiplexer_1_out7), .in(1'b1), .sel(Address_RY[2:0]), .en(enRY));
  Register #(.width(32)) R1 (.D(RY), .en(demultiplexer_1_out0), .Q(R1_q), .clk(clk), .clr(clr));
  Register #(.width(32)) R2 (.D(RY), .en(demultiplexer_1_out1), .Q(R2_q), .clk(clk), .clr(clr));
  Register #(.width(32)) R3 (.D(RY), .en(demultiplexer_1_out2), .Q(R3_q), .clk(clk), .clr(clr));
  Register #(.width(32)) R4 (.D(RY), .en(demultiplexer_1_out3), .Q(R4_q), .clk(clk), .clr(clr));
  Register #(.width(32)) R5 (.D(RY), .en(demultiplexer_1_out4), .Q(R5_q), .clk(clk), .clr(clr));
  Register #(.width(32)) R6 (.D(RY), .en(demultiplexer_1_out5), .Q(R6_q), .clk(clk), .clr(clr));
  Register #(.width(32)) R6_2 (.D(RY), .en(demultiplexer_1_out6), .Q(R6_2_q), .clk(clk), .clr(clr));
  Register #(.width(32)) R7 (.D(RY), .en(demultiplexer_1_out7), .Q(R7_q), .clk(clk), .clr(clr));
  Multiplexer #(.select(3), .width(32)) multiplexer_1 (
    .in0(R1_q), .in1(R2_q), .in2(R3_q), .in3(R4_q), .in4(R5_q), .in5(R6_q), .in6(R6_2_q), .in7(R7_q),
    .out(RA), .sel(Address_RA[2:0]), .en(enRA));
  Multiplexer #(.select(3), .width(32)) multiplexer_2 (
    .in0(R1_q), .in1(R2_q), .in2(R3_q), .in3(R4_q), .in4(R5_q), .in5(R6_q), .in6(R6_2_q), .in7(R7_q),
    .out(RB), .sel(multiplexer_3_out), .en(enRB));
  Multiplexer #(.width(4)) multiplexer_3 (
    .in0(Address_RB), .in1(Address_RY), .out({multiplexer_3_out_2[3], multiplexer_3_out}),
    .sel(SELECT_STORE_MUX), .en(1'b1));

  // Other names for the same wires on the sheet: ADD_RY[3:0] = Address_RY

  // Notes on the sheet:
  //   19CS01065
  //   Register File
endmodule

module ALU (
  input  [31:0] InputRA,
  input  [31:0] InputRB,
  input  ALU_Enable,
  input  [2:0] ALU_Select,
  output [31:0] ALU_Out
);

  wire [31:0] adder_1_out, and_1_out, or_1_out, subtractor_1_out;

  Adder #(.width(32)) adder_1 (.a(InputRA), .b(InputRB), .out(adder_1_out), .cin(1'b0));  // open: cout
  Subtractor #(.width(32)) subtractor_1 (.a(InputRA), .b(InputRB), .out(subtractor_1_out), .bin(1'b0));  // open: bout
  assign and_1_out = InputRA & InputRB;  // AND_Gate and_1, 32 bits wide
  assign or_1_out = InputRA | InputRB;  // OR_Gate or_1, 32 bits wide
  Multiplexer #(.select(3), .width(32)) multiplexer_1 (
    .in0(adder_1_out), .in1(subtractor_1_out), .in2(and_1_out), .in3(or_1_out), .in4(InputRA),
    .in5(adder_1_out), .in6(adder_1_out), .in7(InputRB), .out(ALU_Out), .sel(ALU_Select), .en(ALU_Enable));

  // Notes on the sheet:
  //   19CS01065
  //   ALU
endmodule

module InstructionRegister (
  input  [31:0] INPUT_IR,
  input  EN_IR,
  input  clk,
  input  CLR_IR,
  output [3:0] OPCODE,
  output [3:0] SELECT_RA,
  output [31:0] IMMEDIATE,
  output [3:0] SELECT_RY,
  output [3:0] SELECT_RB
);

  wire [3:0] IR_q;

  Register #(.width(32)) IR (
    .D(INPUT_IR), .en(EN_IR), .Q({OPCODE, SELECT_RY, SELECT_RA, IMMEDIATE[15:0], IR_q}), .clk(clk),
    .clr(CLR_IR));

  assign IMMEDIATE[31:16] = {16{1'b0}};
  assign SELECT_RB = IMMEDIATE[15:12];

  // Notes on the sheet:
  //   19CS01065
  //   IR
endmodule

module ControlUnit (
  input  ADD,
  input  clk,
  input  ADI,
  input  [3:0] OPCODE,
  input  SUB,
  input  SUI,
  input  CLR_CTR,
  input  AND,
  input  ANI,
  input  OR,
  input  ORI,
  input  MOV,
  input  MVI,
  input  LOAD,
  input  STORE,
  input  HLT,
  output Stage_5,
  output Stage_4,
  output out_19,
  output Stage_3,
  output out_21,
  output Stage_2,
  output out_23,
  output Stage_1,
  output out_25,
  output out_26,
  output [2:0] out_27,
  output out_28,
  output out_29,
  output out_30,
  output out_31,
  output out_32,
  output out_33,
  output out_34,
  output out_35,
  output out_36,
  output out_37,
  output out_38
);

  wire and_1_out, NOT_SURE, or_1_out, or_2_out, or_3_out, or_4_out, or_5_out, or_6_out, or_7_out, or_8_out,
       STORE_Select_MUX;
  wire [2:0] counter_1_q;

  and and_1 (and_1_out, Stage_2, HLT);
  or or_1 (or_1_out, ADD, ADI, SUB, SUI, AND, ANI, OR, ORI, MOV, MVI, LOAD, STORE, HLT);
  or or_2 (or_2_out, ADD, SUB, AND, OR, STORE);
  and and_2 (STORE_Select_MUX, Stage_2, STORE);
  not not_1 (out_37, and_1_out);
  or or_3 (or_3_out, LOAD, MOV, ADI, SUI, ANI, ORI);
  Counter #(.width(3), .max('h5)) counter_1 (
    .D(3'b000), .Q(counter_1_q), .clk(clk), .clr(CLR_CTR));  // open: load, count, carry
  and and_3 (out_37, Stage_1, or_1_out);
  and and_4 (out_19, Stage_2, or_2_out);
  and and_5 (out_19, Stage_2, or_3_out);
  Decoder #(.select(3), .enable("false")) decoder_1 (
    .out0(Stage_1), .out1(Stage_2), .out2(Stage_3), .out3(Stage_4), .out4(Stage_5), .sel(counter_1_q));  // open: out5, out6, out7
  or or_4 (or_4_out, MVI, HLT);
  or or_5 (or_5_out, ADD, SUB, AND, MOV, OR, STORE, LOAD, ADI, SUI, ANI, ORI, MVI);
  or or_6 (or_6_out, ADD, SUB, AND, MOV, OR, STORE, LOAD, ADI, SUI, ANI, ORI, MVI);
  or or_7 (or_7_out, ADD, SUB, AND, MOV, OR, STORE, LOAD, ADI, SUI, ANI, ORI, MVI);
  or or_8 (or_8_out, STORE, LOAD, ADI, SUI, ANI, ORI, MVI);
  and and_6 (out_26, Stage_3, or_5_out);
  and and_7 (out_29, Stage_3, or_8_out);
  and and_8 (out_32, Stage_4, or_6_out);
  and and_9 (out_34, Stage_5, or_7_out);
  and and_10 (NOT_SURE, Stage_2, or_4_out);
  and and_11 (out_31, Stage_3, STORE);
  and and_12 (out_33, Stage_4, LOAD);

  assign out_21 = out_19;
  assign out_23 = out_19;
  assign out_25 = out_19;
  assign out_27 = OPCODE[2:0];
  assign out_28 = out_26;
  assign out_30 = out_26;
  assign out_38 = out_37;

  // Other names for the same wires on the sheet: EN_IR = out_37; EN_PC = out_37; EN_RM = out_31; EN_MUX_Y = out_32;
  //   EN_RY = out_32; EN_ALU = out_26; EN_MUX_B = out_26; EN_RZ = out_26; EN_SELECT_MEM = out_36; EN_RA = out_19;
  //   EN_RB = out_19; EN_Select_RA = out_19; EN_Select_RB = out_19; EN_SELECT_RY = out_34;
  //   Select_ALU[2:0] = OPCODE[2:0]; SELECT_MUX_B = out_29; SELECT_MUX_MEM = out_35; SELECT_MUX_Y = out_33

  // Notes on the sheet:
  //   STAGE 1
  //   STAGE 2
endmodule
